# Fritzing sketch 4D_Triceratops (saved by Fritzing 0.9.2b)
breadboards: 1

parts:
  Raspberry_Pi1 = Raspberry Pi 2
  IC1 = L293D [package=THT]
  S1 = Pushbutton [package="[THT]"]
  S2 = Pushbutton [package="[THT]"]
  M2 = DC Motor
  VCC2 = 4 x AAA Battery Mount

nets (from the breadboard view):
  N1: Raspberry_Pi1.GPIO11, S2.Pin_3, S2.Pin_4
  N2: Raspberry_Pi1.GPIO6, IC1.Enable_2
  N3: Raspberry_Pi1.GPIO13, IC1.In_3
  N4: Raspberry_Pi1.GPIO26, S1.Pin_3, S1.Pin_4
  N5: Raspberry_Pi1.GND, IC1.0V, S1.Pin_1, S1.Pin_2, S2.Pin_1, S2.Pin_2, VCC2.-
  N6: Raspberry_Pi1.GPIO16, IC1.In_4
  N7: Raspberry_Pi1.5V, IC1.+V
  N8: IC1.+Vmotor, VCC2.+
  N9: IC1.Out_3_(_Controlled_by_Enable_2_), M2.pin_2
  N10: IC1.Out_4_(_Controlled_by_Enable_2_), M2.pin_1
